# Fritzing sketch v2021-1 (saved by Fritzing 0.9.4)
circuit board: 8.95cm x 2.79893cm
breadboards: 1

parts:
  J5 = female pin header, 19 pins [form="♀ (female)"]
  J4 = female pin header, 19 pins [form="♀ (female)"]
  J6 = longpad pin header, 8 pins [form="long pad"]
  part = Pad [width=3.762962962962963 height=2.445925925925923 connect=center]  # not connected
  part_2 = Pad [width=3.762962962962963 height=2.445925925925923 connect=center]  # not connected

nets:
  N1: J5.pin1, J6.pin1
  N2: J5.pin9, J6.pin8
  N3: J5.pin10, J6.pin7
  N4: J5.pin11, J6.pin6
  N5: J5.pin12, J6.pin3
  N6: J5.pin15, J6.pin4
  N7: J4.pin1, J6.pin2
  N8: J4.pin16, J6.pin5

notes:
  3v3
  thepricedisplay.com
  busy
  rst
  dc
  cs
  clk
  din
  gnd
  vcc
  by bmd
  v2021
  thepricedisplay.com v2021
  bmd
  usb
  esp32 38pin
