# Fritzing sketch Untitled Sketch1 (saved by Fritzing 0.9.4)
circuit board: 5.36516cm x 2.80044cm
breadboards: 1

parts:
  J3 = female pin header, 19 pins [form="♀ (female)"]
  J2 = female pin header, 19 pins [form="♀ (female)"]
  header = female pin header, 4 pins [form="♀ (female)"]
  header1 = female pin header, 4 pins [form="♀ (female)"]

nets:
  N1: J3.pin2, header.pin3
  N2: J3.pin3, header.pin4
  N3: J3.pin6, header1.pin1
  N4: J3.pin9, header1.pin2
  N5: J3.pin10, header1.pin4
  N6: J3.pin13, header1.pin3
  N7: J2.pin1, header.pin1
  N8: J2.pin15, header.pin2

notes:
  thepricedisplay.com
  vcc
  gnd
  3v3
  din
  clk
  cs
  dc
  rst
  busy
  bmd 2021
  v1.0
